# Fritzing sketch TeensyServoDrive (saved by Fritzing 0.9.0b)
perfboards: 1
stripboards: 1

parts:
  Teensy_3_1 = Teensy 3.1  # not connected
  U1 = 7-SEGMENT-4DIGIT [package=7-segment-4digit-youngsun]  # not connected
  U3 = mystery part, 5 pins [chip_label="7 segment"]
  J1 = female pin header, 2 pins [form="♀ (female)"]  # not connected
  J1_2 = female pin header, 2 pins [form="♀ (female)"]  # not connected
  J1_3 = female pin header, 3 pins [form="♀ (female)"]  # not connected
  J2 = female pin header, 4 pins [form="♀ (female)"]
  J3 = female pin header, 4 pins [form="♀ (female)"]  # not connected
  JACK1 = 2.1mm DC Barrel Jack  # not connected

nets:
  N1: U3.pin1, J2.pin3
  N2: U3.pin2, J2.pin4

custom parts:
  Teensy 3.1: The Teensy is a complete USB-based microcontoller development system, in a very small footprint, capable of implementing many types of projects. All programming is done via the USB port. No special programmer is needed, only a standard micro-USB cable and a PC or Macintosh with a USB port. It has a USB keyboard/mouse/joystick emulation stack and can be programmed through Arduino IDE.
  2.1mm DC Barrel Jack: 2.1mm DC Barrel Jack with Thru-Hole Connectors (breadboardable)
